# Fritzing sketch AutonomousRobot-2C (saved by Fritzing 0.9.10b)
breadboards: 1

parts:
  Ultrasonic_Sensor = HC-SR04 Ultrasonic Distance Sensor
  Arduino_Uno_Board = Arduino Uno (Rev3)
  L293D_IC = L293D [package=THT]
  Smoke_Detector = MQ-2 [package="DIP (Dual Inline) [THT]"]
  DC_Motor = gear-motor
  DC_Motor_2 = gear-motor
  9_V = BC9VPC [package=bc9vpc]
  Servo_Motor = Basic Servo
  Buzzer = Piezo Speaker
  Flame_Sensor = KY-026 Flame Sensor Module [package="Breakout board"]

nets:
  VCC: Ultrasonic_Sensor.VCC, Arduino_Uno_Board.5V, L293D_IC.Enable_1, L293D_IC.Enable_2, L293D_IC.+V, Smoke_Detector.pin1, Servo_Motor.vcc, Flame_Sensor.+
  N1: Ultrasonic_Sensor.TRIG, Arduino_Uno_Board.D12/MISO
  N2: Ultrasonic_Sensor.ECHO, Arduino_Uno_Board.D13/SCK
  GND: Ultrasonic_Sensor.GND, Arduino_Uno_Board.GND, L293D_IC.0V, Smoke_Detector.pin2, 9_V.V-, Servo_Motor.gnd, Buzzer.pin1, Flame_Sensor.G
  N3: Arduino_Uno_Board.A2, Smoke_Detector.pin4
  N4: Arduino_Uno_Board.A3, Flame_Sensor.A0
  N5: Arduino_Uno_Board.D9_PWM, L293D_IC.In_3
  N6: Arduino_Uno_Board.D10_PWM/SS, L293D_IC.In_4
  N7: Arduino_Uno_Board.D2, Buzzer.pin2
  N8: Arduino_Uno_Board.D3_PWM, Servo_Motor.pulse
  N9: Arduino_Uno_Board.D5_PWM, L293D_IC.In_1
  N10: Arduino_Uno_Board.D6_PWM, L293D_IC.In_2
  N11: L293D_IC.Out_1_(_Controlled_by_Enable_1_), DC_Motor_2.pin_2
  N12: L293D_IC.Out_2_(_Controlled_by_Enable_1_), DC_Motor_2.pin_1
  N13: L293D_IC.+Vmotor, 9_V.V+
  N14: L293D_IC.Out_3_(_Controlled_by_Enable_2_), DC_Motor.pin_2
  N15: L293D_IC.Out_4_(_Controlled_by_Enable_2_), DC_Motor.pin_1

custom parts:
  MQ-2: MQ-2 Gas Sensor module
  KY-026 Flame Sensor Module: KY-026 Flame Sensor Module reacts in the presence of fire.
